# Fritzing sketch wordclock (saved by Fritzing 0.9.3b)
breadboards: 1

parts:
  U1 = 74AHCT125 [part_number=SN74AHCT125 package=dil14]
  136pcs_WS2812b = ws2812b [package="smd 2812b"]
  Raspberry_Pi_Zero1 = Raspberry Pi Zero
  Power_Supply = DC Power [voltage=5V]
  part = Real Time Clock Module - DS1307 RTC Breakout Board [part_number=.]
  DS2 = DS18B20 1-Wire Temperature Sensor [part_number=DS18B20]
  Pullup = Resistor [tolerance=±5% resistance=4.7k package=THT]
  Pushbutton = Pushbutton [package=THT]

nets:
  GND: U1.1OE, U1.GND, 136pcs_WS2812b.VSS, Raspberry_Pi_Zero1.GND, Power_Supply.V-, part.GND, DS2.GND
  N1: U1.1A, Raspberry_Pi_Zero1.GPIO18
  N2: U1.1Y, 136pcs_WS2812b.DIN
  5V: U1.VCC, 136pcs_WS2812b.VDD, Raspberry_Pi_Zero1.5V, Power_Supply.V+, part.5V
  3V3: Raspberry_Pi_Zero1.3v3, Raspberry_Pi_Zero1.3V3, DS2.VDD, Pullup.Pin_0, Pushbutton.leg1
  N3: Raspberry_Pi_Zero1.GPIO2, part.SDA
  N4: Raspberry_Pi_Zero1.GPIO3, part.SCL
  N5: Raspberry_Pi_Zero1.GPIO4, DS2.DQ, Pullup.Pin_1
  N6: Raspberry_Pi_Zero1.GPIO21, Pushbutton.leg0

notes:
  Remove Pullups from rtc modul!

custom parts:
  74AHCT125: Quad Level-Shifter (3V to 5V) Quadruple Bus Buffer Gates With 3-State Outputs
